// Logisim project SFQ.circ as structural Verilog: 7 circuits, main circuit CLK-AND
module CLK_AND (
  input  in_1,
  input  in_2,
  input  in_3,
  input  in_4,
  output out_5
);

  wire d_ff_1_q, d_ff_2_q, or_1_out;

  or or_1 (or_1_out, in_1, in_4);
  D_Flip_Flop d_ff_1 (.clk(or_1_out), .D(in_2), .Q(d_ff_1_q));  // open: Qn, preset, en, reset
  D_Flip_Flop d_ff_2 (.clk(or_1_out), .D(in_3), .Q(d_ff_2_q));  // open: Qn, preset, en, reset
  and and_1 (out_5, d_ff_1_q, d_ff_2_q);
endmodule

module CLK_NAND (
  input  in_1,
  input  in_2,
  input  in_3,
  input  in_4,
  output out_5
);

  wire d_ff_1_q, d_ff_2_q, or_1_out;

  or or_1 (or_1_out, in_1, in_4);
  D_Flip_Flop d_ff_1 (.clk(or_1_out), .D(in_2), .Q(d_ff_1_q));  // open: Qn, preset, en, reset
  D_Flip_Flop d_ff_2 (.clk(or_1_out), .D(in_3), .Q(d_ff_2_q));  // open: Qn, preset, en, reset
  nand nand_1 (out_5, d_ff_1_q, d_ff_2_q);
endmodule

module CLK_OR (
  input  in_1,
  input  in_2,
  input  in_3,
  input  in_4,
  output out_5
);

  wire d_ff_1_q, d_ff_2_q, or_1_out;

  or or_1 (or_1_out, in_1, in_4);
  D_Flip_Flop d_ff_1 (.clk(or_1_out), .D(in_2), .Q(d_ff_1_q));  // open: Qn, preset, en, reset
  D_Flip_Flop d_ff_2 (.clk(or_1_out), .D(in_3), .Q(d_ff_2_q));  // open: Qn, preset, en, reset
  or or_2 (out_5, d_ff_1_q, d_ff_2_q);
endmodule

module CLK_NOR (
  input  in_1,
  input  in_2,
  input  in_3,
  input  in_4,
  output out_5
);

  wire d_ff_1_q, d_ff_2_q, or_1_out;

  or or_1 (or_1_out, in_1, in_4);
  D_Flip_Flop d_ff_1 (.clk(or_1_out), .D(in_2), .Q(d_ff_1_q));  // open: Qn, preset, en, reset
  D_Flip_Flop d_ff_2 (.clk(or_1_out), .D(in_3), .Q(d_ff_2_q));  // open: Qn, preset, en, reset
  nor nor_1 (out_5, d_ff_1_q, d_ff_2_q);
endmodule

module CLK_NOT (
  input  in_1,
  input  in_2,
  input  in_3,
  output out_4
);

  wire d_ff_1_q, or_1_out;

  or or_1 (or_1_out, in_1, in_3);
  D_Flip_Flop d_ff_1 (.clk(or_1_out), .D(in_2), .Q(d_ff_1_q));  // open: Qn, preset, en, reset
  not not_1 (out_4, d_ff_1_q);
endmodule

module CLK_XOR (
  input  in_1,
  input  in_2,
  input  in_3,
  input  in_4,
  output out_5
);

  wire d_ff_1_q, d_ff_2_q, or_1_out;

  or or_1 (or_1_out, in_1, in_4);
  D_Flip_Flop d_ff_1 (.clk(or_1_out), .D(in_2), .Q(d_ff_1_q));  // open: Qn, preset, en, reset
  D_Flip_Flop d_ff_2 (.clk(or_1_out), .D(in_3), .Q(d_ff_2_q));  // open: Qn, preset, en, reset
  xor xor_1 (out_5, d_ff_1_q, d_ff_2_q);
endmodule

module D_FF (
  input  in_1,
  input  in_2,
  input  in_3,
  output out_4
);

  wire or_1_out;

  or or_1 (or_1_out, in_1, in_3);
  D_Flip_Flop d_ff_1 (.clk(or_1_out), .D(in_2), .Q(out_4));  // open: Qn, preset, en, reset
endmodule
